// Digital circuit SMaC2.dig as structural Verilog
module SMaC2 (
  input  [2:0] SM,
  output [2:0] C2
);

  wire and_1_out, and_2_out, and_3_out, and_4_out, and_5_out, not_1_out, not_2_out, not_3_out;

  not not_1 (not_1_out, SM[2]);
  not not_2 (not_2_out, SM[1]);
  not not_3 (not_3_out, SM[0]);
  and and_1 (and_1_out, SM[2], not_2_out, SM[0]);
  and and_2 (and_2_out, not_1_out, SM[1]);
  and and_3 (and_3_out, SM[1], not_3_out);
  and and_4 (and_4_out, SM[2], SM[0]);
  and and_5 (and_5_out, SM[2], SM[1]);
  or or_1 (C2[1], and_1_out, and_2_out, and_3_out);
  or or_2 (C2[2], and_4_out, and_5_out);

  assign C2[0] = SM[0];
endmodule

/* Test case:
	SM 	C2

	0 	0
	1 	1
	2 	2
	3 	3	
	4 	0
	5 	7
	6 	6
	7 	5
*/
