// Digital circuit solucio.dig as structural Verilog
module solucio (
  input  A2,
  input  A1,
  input  A0,
  input  B2,
  input  B1,
  input  B0,
  input  CA,
  input  CB,
  input  CR,
  output R0,
  output R1,
  output R2
);

  wire comparator_1_eq, comparator_1_gt;
  wire [1:0] or_1_out;
  wire [2:0] multiplexer_1_out, multiplexer_2_out, multiplexer_3_out, smac2_1_c2, smac2_2_c2, smac2_3_c2;

  SMaC2 smac2_1 (.SM({A2, A1, A0}), .C2(smac2_1_c2));
  SMaC2 smac2_2 (.SM({B2, B1, B0}), .C2(smac2_2_c2));
  Multiplexer #(.Bits(3)) multiplexer_1 (.sel(CA), .in_0({A2, A1, A0}), .in_1(smac2_1_c2), .out(multiplexer_1_out));
  Multiplexer #(.Bits(3)) multiplexer_2 (.sel(CB), .in_0({B2, B1, B0}), .in_1(smac2_2_c2), .out(multiplexer_2_out));
  Comparator #(.Signed("true"), .Bits(3)) comparator_1 (
    .a(multiplexer_1_out), .b(multiplexer_2_out), .gt(comparator_1_gt), .eq(comparator_1_eq), .lt(or_1_out[1]));
  or or_1 (or_1_out[0], comparator_1_gt, comparator_1_eq);
  Multiplexer #(.Selector_Bits(2), .Bits(3)) multiplexer_3 (
    .sel(or_1_out), .in_0(3'b000), .in_1(multiplexer_1_out), .in_2(multiplexer_2_out), .in_3(3'b000),
    .out(multiplexer_3_out));
  SMaC2 smac2_3 (.SM(multiplexer_3_out), .C2(smac2_3_c2));
  Multiplexer #(.Bits(3)) multiplexer_4 (.sel(CR), .in_0(multiplexer_3_out), .in_1(smac2_3_c2), .out({R2, R1, R0}));
endmodule

/* Test case:
A2 A1 A0 B2 B1 B0 CA CB CR R2 R1 R0
0 0 0  1 x x  x x x  0 0 0
0 0 1  1 x x  x x x  0 0 1
0 1 0  1 x x  x x x  0 1 0
0 1 1  1 x x  x x x  0 1 1
1 x x  0 0 0  x x x  0 0 0
1 x x  0 0 1  x x x  0 0 1
1 x x  0 1 0  x x x  0 1 0
1 x x  0 1 1  x x x  0 1 1
0 0 0  0 0 0  x x x  0 0 0
0 0 1  0 0 0  x x x  0 0 1
0 1 0  0 0 0  x x x  0 1 0
0 1 1  0 0 0  x x x  0 1 1
0 0 x  0 0 1  x x x  0 0 1
0 1 0  0 0 1  x x x  0 1 0
0 1 1  0 0 1  x x x  0 1 1
0 0 x  0 1 0  x x x  0 1 0
0 1 0  0 1 0  x x x  0 1 0
0 1 1  0 1 0  x x x  0 1 1
0 0 x  0 1 1  x x x  0 1 1
0 1 0  0 1 1  x x x  0 1 1
0 1 1  0 1 1  x x x  0 1 1
1 0 0  1 0 0  0 0 0  1 0 0
1 0 1  1 0 0  0 0 0  1 0 1
1 1 0  1 0 0  0 0 0  1 1 0
1 1 1  1 0 0  0 0 0  1 1 1
1 0 0  1 0 0  0 0 1  x x x
1 0 1  1 0 0  0 0 1  1 1 1
1 1 0  1 0 0  0 0 1  1 1 0
1 1 1  1 0 0  0 0 1  1 0 1
1 0 0  1 0 0  0 1 0  0 0 0
1 0 1  1 0 0  0 1 0  0 0 0
1 1 0  1 0 0  0 1 0  0 0 0
1 1 1  1 0 0  0 1 0  0 0 0
1 0 0  1 0 0  0 1 1  X 0 0
1 0 1  1 0 0  0 1 1  X 0 0
1 1 0  1 0 0  0 1 1  X 0 0
1 1 1  1 0 0  0 1 1  X 0 0
1 0 0  1 0 0  1 0 0  0 0 0
1 0 1  1 0 0  1 0 0  1 1 1
1 1 0  1 0 0  1 0 0  1 1 0
1 1 1  1 0 0  1 0 0  1 0 1
1 0 0  1 0 0  1 0 1  X 0 0
1 0 1  1 0 0  1 0 1  1 0 1
1 1 0  1 0 0  1 0 1  1 1 0
1 1 1  1 0 0  1 0 1  1 1 1
1 0 0  1 0 0  1 1 0  0 0 0
1 0 1  1 0 0  1 1 0  0 0 0
1 1 0  1 0 0  1 1 0  0 0 0
1 1 1  1 0 0  1 1 0  0 0 0
1 0 0  1 0 0  1 1 1  X 0 0
1 0 1  1 0 0  1 1 1  X 0 0
1 1 0  1 0 0  1 1 1  X 0 0 
1 1 1  1 0 0  1 1 1  X 0 0
1 0 0  1 0 1  0 0 0  1 0 1
1 0 1  1 0 1  0 0 0  1 0 1
1 1 0  1 0 1  0 0 0  1 1 0
1 1 1  1 0 1  0 0 0  1 1 1
1 0 0  1 0 1  0 0 1  1 1 1
1 0 1  1 0 1  0 0 1  1 1 1
1 1 0  1 0 1  0 0 1  1 1 0
1 1 1  1 0 1  0 0 1  1 0 1
1 0 0  1 0 1  0 1 0  1 1 1
1 0 1  1 0 1  0 1 0  1 1 1
1 1 0  1 0 1  0 1 0  1 1 1
1 1 1  1 0 1  0 1 0  1 1 1
1 0 0  1 0 1  0 1 1  1 0 1
1 0 1  1 0 1  0 1 1  1 0 1
1 1 0  1 0 1  0 1 1  1 0 1
1 1 1  1 0 1  0 1 1  1 0 1
1 0 0  1 0 1  1 0 0  0 0 0
1 0 1  1 0 1  1 0 0  1 1 1
1 1 0  1 0 1  1 0 0  1 1 0
1 1 1  1 0 1  1 0 0  1 0 1
1 0 0  1 0 1  1 0 1  X 0 0
1 0 1  1 0 1  1 0 1  1 0 1
1 1 0  1 0 1  1 0 1  1 1 0
1 1 1  1 0 1  1 0 1  1 1 1
1 0 0  1 0 1  1 1 0  0 0 0
1 0 1  1 0 1  1 1 0  1 1 1
1 1 0  1 0 1  1 1 0  1 1 1
1 1 1  1 0 1  1 1 0  1 1 1
1 0 0  1 0 1  1 1 1  X 0 0
1 0 1  1 0 1  1 1 1  1 0 1
1 1 0  1 0 1  1 1 1  1 0 1
1 1 1  1 0 1  1 1 1  1 0 1
1 0 0  1 1 0  0 0 0  1 1 0
1 0 1  1 1 0  0 0 0  1 1 0
1 1 0  1 1 0  0 0 0  1 1 0
1 0 0  1 1 0  0 0 1  1 1 0
1 0 1  1 1 0  0 0 1  1 1 0
1 1 0  1 1 0  0 0 1  1 1 0
1 1 1  1 1 0  0 0 1  1 0 1
1 0 0  1 1 0  0 1 0  1 1 0
1 0 1  1 1 0  0 1 0  1 1 0
1 1 0  1 1 0  0 1 0  1 1 0
1 1 1  1 1 0  0 1 0  1 1 1
1 0 0  1 1 0  0 1 1  1 1 0
1 0 1  1 1 0  0 1 1  1 1 0
1 1 0  1 1 0  0 1 1  1 1 0
1 1 1  1 1 0  0 1 1  1 0 1
1 0 0  1 1 0  1 0 0  0 0 0
1 0 1  1 1 0  1 0 0  1 1 1
1 1 0  1 1 0  1 0 0  1 1 0
1 1 1  1 1 0  1 0 0  1 1 0
1 0 0  1 1 0  1 0 1  X 0 0
1 0 1  1 1 0  1 0 1  1 0 1
1 1 0  1 1 0  1 0 1  1 1 0
1 1 1  1 1 0  1 0 1  1 1 0
1 0 0  1 1 0  1 1 0  0 0 0
1 0 1  1 1 0  1 1 0  1 1 1
1 1 0  1 1 0  1 1 0  1 1 0
1 1 1  1 1 0  1 1 0  1 1 0
1 0 0  1 1 0  1 1 1  X 0 0
1 0 1  1 1 0  1 1 1  1 0 1
1 1 0  1 1 0  1 1 1  1 1 0
1 1 1  1 1 0  1 1 1  1 1 0
1 0 0  1 1 1  0 0 0  1 1 1
1 0 1  1 1 1  0 0 0  1 1 1
1 1 0  1 1 1  0 0 0  1 1 1
1 1 1  1 1 1  0 0 0  1 1 1
1 0 0  1 1 1  0 0 1  1 0 1
1 0 1  1 1 1  0 0 1  1 0 1
1 1 0  1 1 1  0 0 1  1 0 1
1 1 1  1 1 1  0 0 1  1 0 1
1 0 0  1 1 1  0 1 0  1 0 1
1 0 1  1 1 1  0 1 0  1 0 1
1 1 0  1 1 1  0 1 0  1 1 0
1 1 1  1 1 1  0 1 0  1 1 1
1 0 0  1 1 1  0 1 1  1 1 1
1 0 1  1 1 1  0 1 1  1 1 1
1 1 0  1 1 1  0 1 1  1 1 0
1 1 1  1 1 1  0 1 1  1 0 1
1 0 0  1 1 1  1 0 0  0 0 0
1 0 1  1 1 1  1 0 0  1 1 1
1 1 0  1 1 1  1 0 0  1 1 1
1 1 1  1 1 1  1 0 0  1 1 1
1 0 0  1 1 1  1 0 1  X 0 0
1 0 1  1 1 1  1 0 1  1 0 1
1 0 1  1 1 1  1 0 1  1 0 1
1 1 0  1 1 1  1 0 1  1 0 1
1 1 1  1 1 1  1 0 1  1 0 1
1 0 0  1 1 1  1 1 0  0 0 0
1 0 1  1 1 1  1 1 0  1 1 1
1 1 0  1 1 1  1 1 0  1 1 0
1 1 1  1 1 1  1 1 0  1 0 1
1 0 0  1 1 1  1 1 1  X 0 0
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*/
