// Digital circuit Display_carga.dig as structural Verilog
module Display_carga (
  input  D0,
  output b,
  output c,
  output d,
  output e,
  output f,
  output a,
  output g
);

  not not_1 (a, D0);

  assign b = 1'b1;
  assign c = 1'b1;
  assign d = a;
  assign e = a;
  assign f = a;
  assign g = 1'b0;
endmodule
