// Digital circuit Display_pisos.dig as structural Verilog
module Display_pisos (
  input  D2,
  input  D1,
  output a,
  output b,
  output c,
  output d,
  output e,
  output f,
  output g
);

  not not_1 (c, D2);
  not not_2 (a, D1);
  and and_1 (f, a, c);

  assign b = 1'b1;
  assign d = a;
  assign e = a;
  assign g = D2;
endmodule
