// Digital circuit FFL_0.dig as structural Verilog
module FFL_0 (
  input  x2,
  input  x1,
  input  x0,
  input  CLK,
  output Q0,
  output Q_0
);

  wire and_1_out, and_2_out, and_3_out, not_1_out, or_1_out;

  not not_1 (not_1_out, x2);
  and and_1 (and_1_out, Q0, not_1_out);
  and and_2 (and_2_out, Q0, x0);
  and and_3 (and_3_out, not_1_out, x1, x0);
  or or_1 (or_1_out, and_1_out, and_2_out, and_3_out);
  D_FF d_ff_1 (.D(or_1_out), .C(CLK), .Q(Q0), .nQ(Q_0));
endmodule
