// Digital circuit FFL_2.dig as structural Verilog
module FFL_2 (
  input  x2,
  input  x1,
  input  x0,
  input  CLK,
  output Q2,
  output Q2_2
);

  wire and_1_out, and_2_out, and_3_out, not_1_out, not_2_out, or_1_out;

  not not_1 (not_1_out, x1);
  not not_2 (not_2_out, x0);
  and and_1 (and_1_out, Q2, x1);
  and and_2 (and_2_out, Q2, x2);
  and and_3 (and_3_out, x1, not_2_out);
  or or_1 (or_1_out, and_1_out, and_2_out, and_3_out);
  D_FF d_ff_1 (.D(or_1_out), .C(CLK), .Q(Q2), .nQ(Q2_2));
endmodule
