// Digital circuit M.dig as structural Verilog
module M (
  input  x2,
  input  x1,
  input  x0,
  input  Q2,
  input  Q1,
  output M
);

  wire and_1_out, and_2_out, and_3_out, and_4_out, not_1_out, not_2_out, not_3_out, not_4_out, not_5_out;

  not not_1 (not_1_out, x2);
  not not_2 (not_2_out, x1);
  not not_3 (not_3_out, x0);
  not not_4 (not_4_out, Q2);
  not not_5 (not_5_out, Q1);
  and and_1 (and_1_out, not_5_out, not_2_out, x0);
  and and_2 (and_2_out, not_4_out, x1, not_3_out);
  and and_3 (and_3_out, Q1, not_1_out, not_3_out);
  and and_4 (and_4_out, Q2, not_1_out, not_2_out);
  or or_1 (M, and_1_out, and_2_out, and_3_out, and_4_out);
endmodule
