// Digital circuit P0_P1.dig as structural Verilog
module P0_P1 (
  input  x1,
  input  x0,
  input  Q2,
  input  Q1,
  output P0,
  output P1
);

  wire and_1_out, not_1_out, not_2_out, not_3_out, not_4_out;

  not not_1 (not_1_out, x1);
  not not_2 (not_2_out, x0);
  not not_3 (not_3_out, Q2);
  not not_4 (not_4_out, Q1);
  and and_1 (and_1_out, not_3_out, not_4_out);
  and and_2 (P0, not_4_out, not_2_out);
  or or_1 (P1, x1, and_1_out);
endmodule
