// Digital circuit solucio.dig as structural Verilog
module solucio (
  input  X2,
  input  X1,
  input  X0,
  input  CLK,
  output M,
  output P0,
  output P1,
  output Q1,
  output Q2,
  output Q0
);

  wire \Display_indicador_càrrega_a , \Display_indicador_càrrega_b , \Display_indicador_càrrega_c ,
       \Display_indicador_càrrega_d , \Display_indicador_càrrega_e , \Display_indicador_càrrega_f ,
       \Display_indicador_càrrega_g , Display_indicador_Pis_a, Display_indicador_Pis_b,
       Display_indicador_Pis_c, Display_indicador_Pis_d, Display_indicador_Pis_e, Display_indicador_Pis_f,
       Display_indicador_Pis_g;

  FFL_2 Flip_Flop_D2 (.x2(X2), .x1(X1), .x0(X0), .CLK(CLK), .Q2(Q2));  // open: Q2_2
  FFL_1 Flip_Flop_D1 (.x2(X2), .x1(X1), .x0(X0), .CLK(CLK), .Q1(Q1));  // open: Q_1
  FFL_0 Flip_Flop_D0 (.x2(X2), .x1(X1), .x0(X0), .CLK(CLK), .Q0(Q0));  // open: Q_0
  P0_P1 P1_P0 (.x1(X1), .x0(X0), .Q2(Q2), .Q1(Q1), .P0(P0), .P1(P1));
  M u_M (.x2(X2), .x1(X1), .x0(X0), .Q2(Q2), .Q1(Q1), .M(M));
  Display_pisos Display_indicador_Pis (
    .D2(Q2), .D1(Q1), .a(Display_indicador_Pis_a), .b(Display_indicador_Pis_b), .c(Display_indicador_Pis_c),
    .d(Display_indicador_Pis_d), .e(Display_indicador_Pis_e), .f(Display_indicador_Pis_f),
    .g(Display_indicador_Pis_g));
  Display_carga \Display_indicador_càrrega  (
    .D0(Q0), .b(\Display_indicador_càrrega_b ), .c(\Display_indicador_càrrega_c ),
    .d(\Display_indicador_càrrega_d ), .e(\Display_indicador_càrrega_e ), .f(\Display_indicador_càrrega_f ),
    .a(\Display_indicador_càrrega_a ), .g(\Display_indicador_càrrega_g ));
  Seven_Seg seven_seg_1 (
    .a(Display_indicador_Pis_a), .b(Display_indicador_Pis_b), .c(Display_indicador_Pis_c),
    .d(Display_indicador_Pis_d), .e(Display_indicador_Pis_e), .f(Display_indicador_Pis_f),
    .g(Display_indicador_Pis_g), .dp(1'b1));
  Seven_Seg seven_seg_2 (
    .a(\Display_indicador_càrrega_a ), .b(\Display_indicador_càrrega_b ), .c(\Display_indicador_càrrega_c ),
    .d(\Display_indicador_càrrega_d ), .e(\Display_indicador_càrrega_e ), .f(\Display_indicador_càrrega_f ),
    .g(\Display_indicador_càrrega_g ), .dp(1'b1));
endmodule

/* Test case:
CLK	Q2	Q1	Q0	X2	X1	X0
0	0	0	0	0	0	0
c	1	0	0	0	1	0
c	0	1	0	0	0	1
c	0	0	0	0	0	0
c	0	1	0	0	0	1
c	1	0	0	0	1	0
c	0	0	0	0	0	0
c	0	0	1	0	1	1
c	0	0	0	1	0	0
c	0	1	0	0	0	1
c	0	1	1	0	1	1
c	0	1	0	1	0	0
c	1	0	0	0	1	0
c	1	0	1	0	1	1
c	1	0	0	1	0	0
c	1	0	1	0	1	1
c	0	1	1	0	0	1
c	0	0	1	0	0	0
c	0	1	1	0	0	1
c	1	0	1	0	1	0
c	0	0	1	0	0	0
c	1	0	1	0	1	0
*/
